// Logisim project Domaci2.circ as structural Verilog: 3 circuits, main circuit main
module main (
  input  x1,
  input  x2,
  input  x3,
  input  x4,
  input  x5,
  output f
);

  wire and_1_out, and_2_out, and_4_out, not_1_out, not_2_out, not_3_out;

  not not_1 (not_1_out, x1);
  and and_1 (and_1_out, not_1_out, x2);
  not not_2 (not_2_out, x3);
  not not_3 (not_3_out, x4);
  and and_2 (and_2_out, and_1_out, not_2_out);
  and and_3 (f, and_2_out, and_4_out);
  and and_4 (and_4_out, not_3_out, x5);

  // Notes on the sheet:
  //   31.05.
  //   3+1+5=9
  //   01001 = 9
endmodule

module NILI (
  input  x1,
  input  x2,
  input  x3,
  input  x4,
  input  x5,
  output f
);

  wire nor_1_out, nor_2_out, nor_3_out, nor_4_out, nor_5_out, nor_6_out, nor_7_out, nor_8_out, nor_9_out,
       nor_10_out, nor_11_out, nor_12_out, nor_13_out, nor_14_out;

  nor nor_1 (nor_1_out, x1, x1);
  nor nor_2 (nor_2_out, x4, x4);
  nor nor_3 (nor_3_out, nor_1_out, nor_1_out);
  nor nor_4 (nor_4_out, x2, x2);
  nor nor_5 (nor_5_out, nor_2_out, nor_2_out);
  nor nor_6 (nor_6_out, x5, x5);
  nor nor_7 (nor_7_out, nor_3_out, nor_4_out);
  nor nor_8 (nor_8_out, x3, x3);
  nor nor_9 (nor_9_out, nor_7_out, nor_7_out);
  nor nor_10 (nor_10_out, nor_8_out, nor_8_out);
  nor nor_11 (nor_11_out, nor_9_out, nor_10_out);
  nor nor_12 (nor_12_out, nor_5_out, nor_6_out);
  nor nor_13 (nor_13_out, nor_11_out, nor_11_out);
  nor nor_14 (nor_14_out, nor_12_out, nor_12_out);
  nor nor_15 (f, nor_13_out, nor_14_out);
endmodule

module Konacno (
  input  x1,
  input  x2,
  input  x3,
  input  x4,
  input  x5,
  output f
);

  wire nor_1_out, nor_2_out, nor_3_out, nor_4_out, nor_5_out, nor_6_out, nor_7_out, nor_8_out;

  nor nor_1 (nor_1_out, x2, x2);
  nor nor_2 (nor_2_out, x5, x5);
  nor nor_3 (nor_3_out, x1, nor_1_out);
  nor nor_4 (nor_4_out, nor_3_out, nor_3_out);
  nor nor_5 (nor_5_out, nor_4_out, x3);
  nor nor_6 (nor_6_out, x4, nor_2_out);
  nor nor_7 (nor_7_out, nor_5_out, nor_5_out);
  nor nor_8 (nor_8_out, nor_6_out, nor_6_out);
  nor nor_9 (f, nor_7_out, nor_8_out);
endmodule
